// Logisim project cpu_test.circ as structural Verilog: 6 circuits, main circuit ALU
module main (
  input  in_1
);

  wire and_1_out, clk, clock_1_out, comparator_1_eq, not_1_out;
  wire [1:1] registerfile_1_d1_2;
  wire [3:0] multiplexer_2_out;
  wire [6:0] registerfile_1_d1;
  wire [7:0] alu_1_result, InstructionMemory_data, memorymodule_1_dataout, memorymodule_1_outputport,
       multiplexer_3_out, multiplexer_4_out, programcounter_1_instructionaddr, registerfile_1_d2;
  wire [15:0] ControlRom_data;
  wire [15:8] InstructionMemory_data_2;

  ProgramCounter programcounter_1 (
    .Reset(in_1), .Load(and_1_out), .Enable(ControlRom_data[1]), .Clock(clk),
    .InputAddr(InstructionMemory_data), .InstructionAddr(programcounter_1_instructionaddr));
  Hex_Digit_Display hex_digit_display_1 (.value(programcounter_1_instructionaddr[7:4]));  // open: dp
  ROM #(.dataWidth(16)) InstructionMemory (
    .addr(programcounter_1_instructionaddr), .data({InstructionMemory_data_2, InstructionMemory_data}));
  Hex_Digit_Display hex_digit_display_2 (.value(programcounter_1_instructionaddr[3:0]));  // open: dp
  Multiplexer multiplexer_1 (.in0(1'b0), .in1(clock_1_out), .out(clk), .sel(ControlRom_data[1]));
  Clock clock_1 (.out(clock_1_out));
  and and_1 (and_1_out, registerfile_1_d1_2[1], ControlRom_data[8]);
  ROM #(.addrWidth(4), .dataWidth(16)) ControlRom (.addr(InstructionMemory_data_2[15:12]), .data(ControlRom_data));
  Multiplexer #(.width(4)) multiplexer_2 (
    .in0(InstructionMemory_data[3:0]), .in1(InstructionMemory_data_2[11:8]), .out(multiplexer_2_out),
    .sel(ControlRom_data[4]));
  Multiplexer #(.width(8)) multiplexer_3 (
    .in0(multiplexer_4_out), .in1(InstructionMemory_data), .out(multiplexer_3_out), .sel(ControlRom_data[3]));
  Multiplexer #(.width(8)) multiplexer_4 (
    .in0(alu_1_result), .in1(memorymodule_1_dataout), .out(multiplexer_4_out), .sel(ControlRom_data[9]));
  RegisterFile registerfile_1 (
    .Data(multiplexer_3_out), .Enable(ControlRom_data[2]), .Clock(clk), .Write(multiplexer_2_out),
    .R1(InstructionMemory_data_2[11:8]), .R2(InstructionMemory_data[7:4]),
    .D1({registerfile_1_d1[6:1], registerfile_1_d1_2[1], registerfile_1_d1[0]}), .D2(registerfile_1_d2));
  ALU alu_1 (
    .A({registerfile_1_d1[6:1], registerfile_1_d1_2[1], registerfile_1_d1[0]}), .B(registerfile_1_d2),
    .SETTING(ControlRom_data[7:5]), .RESULT(alu_1_result));
  MemoryModule memorymodule_1 (
    .Address(InstructionMemory_data), .Store(ControlRom_data[0]), .Clk(clk),
    .DataIn({registerfile_1_d1[6:1], registerfile_1_d1_2[1], registerfile_1_d1[0]}),
    .DataOut(memorymodule_1_dataout), .OutputPort(memorymodule_1_outputport));  // open: InputPort
  Hex_Digit_Display hex_digit_display_3 (.value(memorymodule_1_outputport[7:4]));  // open: dp
  Hex_Digit_Display hex_digit_display_4 (.value(memorymodule_1_outputport[3:0]));  // open: dp
  TTY #(.trigger("falling")) tty_1 (
    .data(memorymodule_1_outputport[6:0]), .clk(clk), .we(not_1_out), .clr(memorymodule_1_outputport[7]));
  not not_1 (not_1_out, comparator_1_eq);
  Comparator comparator_1 (.a(memorymodule_1_outputport), .b({8{1'b0}}), .eq(comparator_1_eq));  // open: gt, lt

  // Notes on the sheet:
  //   contents of InstructionMemory (hex, n*v repeats v):
  //   a180 d100 d101 a148 d101 d001 a165 d101 d001 a16c d101 d001 a16c d101 d001 a16f d101 d001 a120 d101
  //   d001 1000
  //   contents of ControlRom (hex, n*v repeats v):
  //   2 0 6 26 46 66 86 a6 c6 e6 1e 106 806 3
endmodule

module ALU (
  input  [7:0] A,
  input  [7:0] B,
  input  [2:0] SETTING,
  output [7:0] RESULT
);

  wire [2:0] comparator_1_gt;
  wire [7:0] adder_1_out, and_1_out, not_1_out, or_1_out, shifter_1_out, subtractor_1_out, xor_1_out;

  Adder adder_1 (.a(A), .b(B), .out(adder_1_out));  // open: cin, cout
  Subtractor subtractor_1 (.a(A), .b(B), .out(subtractor_1_out));  // open: bin, bout
  assign or_1_out = A | B;  // OR_Gate or_1, 8 bits wide
  assign and_1_out = A & B;  // AND_Gate and_1, 8 bits wide
  assign xor_1_out = A ^ B;  // XOR_Gate xor_1, 8 bits wide
  assign not_1_out = ~A;  // NOT_Gate not_1, 8 bits wide
  Shifter #(.shift("lr")) shifter_1 (.in(A), .\dist (3'b001), .out(shifter_1_out));
  Comparator comparator_1 (.a(A), .b(B), .gt(comparator_1_gt[0]), .eq(comparator_1_gt[1]), .lt(comparator_1_gt[2]));
  Multiplexer #(.select(3), .width(8)) multiplexer_1 (
    .in0(adder_1_out), .in1(subtractor_1_out), .in2(or_1_out), .in3(and_1_out), .in4(xor_1_out),
    .in5(not_1_out), .in6(shifter_1_out), .in7({{5{1'b0}}, comparator_1_gt}), .out(RESULT), .sel(SETTING));

  // Notes on the sheet:
  //   B: initial=0x1
  //   A: initial=0x1
  //   Setting order is top to bottom from 0-7
  //   Invalid Settings Return 0x00
endmodule

module RegisterFile (
  input  [7:0] Data,
  input  Enable,
  input  Clock,
  input  [3:0] Write,
  input  [3:0] R1,
  input  [3:0] R2,
  output [7:0] D1,
  output [7:0] D2
);

  wire demultiplexer_1_out1, demultiplexer_1_out2, demultiplexer_1_out3, demultiplexer_1_out4,
       demultiplexer_1_out5, demultiplexer_1_out6, demultiplexer_1_out7, demultiplexer_1_out8,
       demultiplexer_1_out9, demultiplexer_1_out10, demultiplexer_1_out11, demultiplexer_1_out12,
       demultiplexer_1_out13, demultiplexer_1_out14, demultiplexer_1_out15;
  wire [7:0] dualregister_1_out1, dualregister_1_out2, dualregister_2_out1, dualregister_2_out2,
       dualregister_3_out1, dualregister_3_out2, dualregister_4_out1, dualregister_4_out2,
       dualregister_5_out1, dualregister_5_out2, dualregister_6_out1, dualregister_6_out2,
       dualregister_7_out1, dualregister_7_out2, dualregister_8_out1, dualregister_8_out2,
       dualregister_9_out1, dualregister_9_out2, dualregister_10_out1, dualregister_10_out2,
       dualregister_11_out1, dualregister_11_out2, dualregister_12_out1, dualregister_12_out2,
       dualregister_13_out1, dualregister_13_out2, dualregister_14_out1, dualregister_14_out2,
       dualregister_15_out1, dualregister_15_out2;

  Demultiplexer #(.enable("true"), .select(4)) demultiplexer_1 (
    .out1(demultiplexer_1_out1), .out2(demultiplexer_1_out2), .out3(demultiplexer_1_out3),
    .out4(demultiplexer_1_out4), .out5(demultiplexer_1_out5), .out6(demultiplexer_1_out6),
    .out7(demultiplexer_1_out7), .out8(demultiplexer_1_out8), .out9(demultiplexer_1_out9),
    .out10(demultiplexer_1_out10), .out11(demultiplexer_1_out11), .out12(demultiplexer_1_out12),
    .out13(demultiplexer_1_out13), .out14(demultiplexer_1_out14), .out15(demultiplexer_1_out15), .in(Clock),
    .sel(Write), .en(Enable));  // open: out0
  DualRegister dualregister_1 (
    .Data(Data), .Clock(demultiplexer_1_out1), .OUT1(dualregister_1_out1), .OUT2(dualregister_1_out2));
  DualRegister dualregister_2 (
    .Data(Data), .Clock(demultiplexer_1_out2), .OUT1(dualregister_2_out1), .OUT2(dualregister_2_out2));
  DualRegister dualregister_3 (
    .Data(Data), .Clock(demultiplexer_1_out3), .OUT1(dualregister_3_out1), .OUT2(dualregister_3_out2));
  DualRegister dualregister_4 (
    .Data(Data), .Clock(demultiplexer_1_out4), .OUT1(dualregister_4_out1), .OUT2(dualregister_4_out2));
  DualRegister dualregister_5 (
    .Data(Data), .Clock(demultiplexer_1_out5), .OUT1(dualregister_5_out1), .OUT2(dualregister_5_out2));
  DualRegister dualregister_6 (
    .Data(Data), .Clock(demultiplexer_1_out6), .OUT1(dualregister_6_out1), .OUT2(dualregister_6_out2));
  DualRegister dualregister_7 (
    .Data(Data), .Clock(demultiplexer_1_out7), .OUT1(dualregister_7_out1), .OUT2(dualregister_7_out2));
  DualRegister dualregister_8 (
    .Data(Data), .Clock(demultiplexer_1_out8), .OUT1(dualregister_8_out1), .OUT2(dualregister_8_out2));
  DualRegister dualregister_9 (
    .Data(Data), .Clock(demultiplexer_1_out9), .OUT1(dualregister_9_out1), .OUT2(dualregister_9_out2));
  DualRegister dualregister_10 (
    .Data(Data), .Clock(demultiplexer_1_out10), .OUT1(dualregister_10_out1), .OUT2(dualregister_10_out2));
  DualRegister dualregister_11 (
    .Data(Data), .Clock(demultiplexer_1_out11), .OUT1(dualregister_11_out1), .OUT2(dualregister_11_out2));
  DualRegister dualregister_12 (
    .Data(Data), .Clock(demultiplexer_1_out12), .OUT1(dualregister_12_out1), .OUT2(dualregister_12_out2));
  DualRegister dualregister_13 (
    .Clock(demultiplexer_1_out13), .OUT1(dualregister_13_out1), .OUT2(dualregister_13_out2));  // open: Data
  DualRegister dualregister_14 (
    .Data(Data), .Clock(demultiplexer_1_out14), .OUT1(dualregister_14_out1), .OUT2(dualregister_14_out2));
  DualRegister dualregister_15 (
    .Data(Data), .Clock(demultiplexer_1_out15), .OUT1(dualregister_15_out1), .OUT2(dualregister_15_out2));
  Multiplexer #(.enable("true"), .select(4), .width(8)) multiplexer_1 (
    .in0({8{1'b0}}), .in1(dualregister_1_out2), .in2(dualregister_2_out2), .in3(dualregister_3_out2),
    .in4(dualregister_4_out2), .in5(dualregister_5_out2), .in6(dualregister_6_out2),
    .in7(dualregister_7_out2), .in8(dualregister_8_out2), .in9(dualregister_9_out2),
    .in10(dualregister_10_out2), .in11(dualregister_11_out2), .in12(dualregister_12_out2),
    .in13(dualregister_13_out2), .in14(dualregister_14_out2), .in15(dualregister_15_out2), .out(D2),
    .sel(R2), .en(Enable));
  Multiplexer #(.select(4), .width(8)) multiplexer_2 (
    .in0({8{1'b0}}), .in1(dualregister_1_out1), .in2(dualregister_2_out1), .in3(dualregister_3_out1),
    .in4(dualregister_4_out1), .in5(dualregister_5_out1), .in6(dualregister_6_out1),
    .in7(dualregister_7_out1), .in8(dualregister_8_out1), .in9(dualregister_9_out1),
    .in10(dualregister_10_out1), .in11(dualregister_11_out1), .in12(dualregister_12_out1),
    .in13(dualregister_13_out1), .in14(dualregister_14_out1), .in15(dualregister_15_out1), .out(D1), .sel(R1));
endmodule

module DualRegister (
  input  [7:0] Data,
  input  Clock,
  output [7:0] OUT1,
  output [7:0] OUT2
);

  Register #(.trigger("falling")) register_1 (.D(Data), .clk(Clock), .Q(OUT1));  // open: en, clr
  Register #(.trigger("falling")) register_2 (.D(Data), .clk(Clock), .Q(OUT2));  // open: en, clr
endmodule

module ProgramCounter (
  input  Reset,
  input  Load,
  input  Enable,
  input  Clock,
  input  [7:0] InputAddr,
  output [7:0] InstructionAddr
);

  Counter #(.trigger("falling")) counter_1 (
    .clr(Reset), .load(Load), .count(Enable), .clk(Clock), .D(InputAddr), .Q(InstructionAddr));  // open: up, carry
endmodule

module MemoryModule (
  input  [7:0] InputPort,
  input  Store,
  input  [7:0] DataIn,
  input  [7:0] Address,
  input  Clk,
  output [7:0] DataOut,
  output [7:0] OutputPort
);

  wire demultiplexer_1_out0, demultiplexer_1_out1, demultiplexer_1_out2, demultiplexer_1_out3, not_1_out,
       or_1_out, xor_1_out;
  wire [1:0] multiplexer_1_out;
  wire [7:0] demultiplexer_2_out0, demultiplexer_2_out1, demultiplexer_2_out2, ram_1_dout, register_1_q,
       register_3_q;

  xor xor_1 (xor_1_out, Address[0], Address[1]);
  and and_1 (multiplexer_1_out[1], xor_1_out, ~Address[2], ~Address[3], ~Address[4], ~Address[5], ~Address[6], ~Address[7], ~register_1_q[0], ~register_1_q[1], ~register_1_q[2], ~register_1_q[3], ~register_1_q[4], ~register_1_q[5], ~register_1_q[6], register_1_q[7]);  // AND_Gate
  Multiplexer multiplexer_1 (.in0(or_1_out), .in1(not_1_out), .out(multiplexer_1_out[0]), .sel(multiplexer_1_out[1]));
  not not_1 (not_1_out, Address[0]);
  or or_1 (or_1_out, Address[0], Address[1], Address[2], Address[3], Address[4], Address[5], Address[6], Address[7]);
  Demultiplexer #(.select(2)) demultiplexer_1 (
    .out0(demultiplexer_1_out0), .out1(demultiplexer_1_out1), .out2(demultiplexer_1_out2),
    .out3(demultiplexer_1_out3), .in(Store), .sel(multiplexer_1_out));
  Demultiplexer #(.select(2), .width(8)) demultiplexer_2 (
    .out0(demultiplexer_2_out0), .out1(demultiplexer_2_out1), .out2(demultiplexer_2_out2), .in(DataIn),
    .sel(multiplexer_1_out));  // open: out3
  Register #(.trigger("falling")) register_1 (
    .D(demultiplexer_2_out0), .en(demultiplexer_1_out0), .clk(Clk), .Q(register_1_q));  // open: clr
  RAM #(.addrWidth(16), .trigger("falling")) ram_1 (
    .addr({register_1_q, Address}), .we(demultiplexer_1_out1), .oe(1'b1), .clk(Clk),
    .din(demultiplexer_2_out1), .dout(ram_1_dout));
  Multiplexer #(.select(2), .width(8)) multiplexer_2 (
    .in0(register_1_q), .in1(ram_1_dout), .in3(register_3_q), .out(DataOut), .sel(multiplexer_1_out));  // open: in2
  Register register_2 (.D(demultiplexer_2_out2), .en(demultiplexer_1_out2), .clk(Clk), .Q(OutputPort));  // open: clr
  Register register_3 (.D(InputPort), .en(demultiplexer_1_out3), .clk(Clk), .Q(register_3_q));  // open: clr
endmodule
